# Fritzing sketch PainelSolar (saved by Fritzing 0.9.2b)
breadboards: 1

parts:
  Componente1 = Arduino Uno (Rev3) - ICSP
  Componente2 = Solar Cell
  R1 = Photocell (LDR) [package=THT]
  R2 = Photocell (LDR) [package=THT]
  R3 = Resistor [tolerance=±5% resistance=10k package=THT]
  R4 = Resistor [tolerance=±5% resistance=10k package=THT]
  J1 = Basic Servo

nets:
  N1: Componente1.A0, R1.pin_0, R4.Pin_1
  N2: Componente1.A1, R2.pin_0, R3.Pin_1
  N3: Componente1.A2, Componente2.+
  GND: Componente1.GND, Componente2.-, R2.pin_1, J1.gnd
  N4: Componente1.D5_PWM, J1.pulse
  5V: Componente1.5V, R3.Pin_0, R4.Pin_0, J1.vcc

notes:
  5
  Todos os fios pretos se conectam ao GND e todos os vermelhos ao 5V
  A0 - A2
